// Logisim project 32bit_bat_joystick.circ as structural Verilog: 4 circuits, main circuit main
module main (
);

  wire clock_1_out, clock_2_out, L_out, R_out;
  wire [3:0] joystick_1_x;
  wire [31:0] random_1_out, shift_1_out_3, undriven;

  Controlled_Inverter controlled_inverter_1 ();  // open: in, out, en
  Clock clock_1 (.out(clock_1_out));
  Joystick joystick_1 (.x(joystick_1_x));  // open: y
  // Probe on joystick_1_x
  Button L (.out(L_out));
  Clock clock_2 (.out(clock_2_out));
  Random #(.width(32)) random_1 (.clk(clock_1_out), .out(random_1_out));  // open: next, clr
  Button R (.out(R_out));
  DotMatrix #(.inputtype("row"), .matrixcols(32), .matrixrows(32)) dotmatrix_1 (
    .row6(undriven), .row7(undriven), .row8(undriven), .row9(undriven), .row10(undriven), .row11(undriven),
    .row31(shift_1_out_3));  // open: row0, row1, row2, row3, row4, row5, row12, row13, row14, row15, row16, row17, row18, row19, row20, row21, row22, row23, row24, row25, row26, row27, row28, row29, row30
  shift shift_1 (.in_1(joystick_1_x), .clock(clock_2_out), .out_3(shift_1_out_3));
  Multiplexer multiplexer_1 ();  // open: in0, in1, out, sel, en
  Register register_1 ();  // open: D, en, Q, clk, clr
  Counter counter_1 ();  // open: load, D, count, Q, carry, clk, clr
  Demultiplexer demultiplexer_1 ();  // open: out0, out1, in, sel, en
  BitAdder bitadder_1 ();  // open: in0, out
endmodule

module shift (
  input  [3:0] in_1,
  input  clock,
  output [31:0] out_3
);

  wire and_1_out, comparator_2_eq, comparator_3_eq, comparator_4_eq, l_or_r, left_cnt, left_comp, or_1_out,
       or_2_out, right_cnt, right_comp, trigger;
  wire [31:0] multiplexer_1_out, multiplexer_3_out, multiplexer_4_out, register_1_q, shift, shifter_1_out,
       shifter_2_out;

  Comparator #(.width(4), .mode("unsigned")) comparator_1 (
    .a(in_1), .b(4'b1000), .gt(right_cnt), .lt(left_cnt));  // open: eq
  or or_1 (or_1_out, left_cnt, right_cnt);
  Shifter #(.width(32), .shift("lr")) shifter_1 (.in(multiplexer_4_out), .\dist (5'b00001), .out(shifter_1_out));
  Shifter #(.width(32)) shifter_2 (.in(multiplexer_4_out), .\dist (5'b00001), .out(shifter_2_out));
  or or_2 (or_2_out, right_cnt, left_cnt);
  Register #(.width(32)) register_1 (.D(shift), .Q(register_1_q), .clk(and_1_out));  // open: en, clr
  and and_1 (and_1_out, clock, l_or_r);
  // NOT_Gate not_1 has open pins: in=or_1_out, out=open
  Comparator #(.width(32), .mode("unsigned")) comparator_2 (
    .a(32'hf), .b(shifter_1_out), .eq(comparator_2_eq));  // open: gt, lt
  Comparator #(.width(32), .mode("unsigned")) comparator_3 (
    .a(shifter_2_out), .b(32'hf0000000), .eq(comparator_3_eq));  // open: gt, lt
  D_Flip_Flop d_ff_1 (.clk(or_2_out), .D(1'b1), .Q(trigger));  // open: Qn, preset, en, reset
  // Probe on nothing
  Multiplexer #(.width(32), .enable("false")) multiplexer_1 (
    .in0(shifter_1_out), .in1(32'h1f), .out(multiplexer_1_out), .sel(comparator_2_eq));
  Multiplexer #(.width(32), .enable("false")) multiplexer_2 (
    .in0(multiplexer_1_out), .in1(multiplexer_3_out), .out(shift), .sel(left_cnt));
  Multiplexer #(.width(32), .enable("false")) multiplexer_3 (
    .in0(shifter_2_out), .in1(32'hf8000000), .out(multiplexer_3_out), .sel(comparator_3_eq));
  // Probe on nothing
  or or_3 (l_or_r, left_cnt, right_cnt);
  Comparator #(.width(32)) comparator_4 (.a({32{1'b0}}), .b(register_1_q), .eq(comparator_4_eq));  // open: gt, lt
  // AND_Gate and_2 has open pins: in0=l_or_r, in1=trigger, out=open
  Multiplexer #(.width(32), .enable("false")) multiplexer_4 (
    .in0(register_1_q), .in1(32'h7c000), .out(multiplexer_4_out), .sel(comparator_4_eq));
  Multiplexer #(.width(32), .enable("false")) multiplexer_5 (
    .in0(register_1_q), .in1(32'h7c000), .out(out_3), .sel(comparator_4_eq));
  Comparator #(.width(32), .mode("unsigned")) comparator_5 (.a({32{1'b0}}), .b(out_3), .eq(left_comp));  // open: gt, lt
  Comparator #(.width(32), .mode("unsigned")) comparator_6 (.a(32'h1), .b(out_3), .eq(right_comp));  // open: gt, lt

  // Notes on the sheet:
  //   left
  //   right
endmodule

module shift_left (
  input  left,
  output [4:0] out_2
);

  wire comparator_1_eq, left_comp, or_1_out;
  wire [4:0] multiplexer_1_out, register_1_q, shift;

  buf or_1 (or_1_out, left);  // OR_Gate
  Register #(.width(5)) register_1 (.D(shift), .Q(register_1_q), .clk(or_1_out));  // open: en, clr
  Shifter #(.width(5)) shifter_1 (.in(multiplexer_1_out), .\dist (3'b001), .out(shift));
  Comparator #(.width(5)) comparator_1 (.a({5{1'b0}}), .b(register_1_q), .eq(comparator_1_eq));  // open: gt, lt
  Multiplexer #(.width(5), .enable("false")) multiplexer_1 (
    .in0(register_1_q), .in1(5'b00100), .out(multiplexer_1_out), .sel(comparator_1_eq));
  Multiplexer #(.width(5), .enable("false")) multiplexer_2 (
    .in0(register_1_q), .in1(5'b00100), .out(out_2), .sel(comparator_1_eq));
  Comparator #(.width(5), .mode("unsigned")) comparator_2 (.a(5'b10000), .b(out_2), .eq(left_comp));  // open: gt, lt
endmodule

module shift_right (
  input  right,
  output [4:0] out_2
);

  wire comparator_1_eq, left_comp, or_1_out;
  wire [4:0] multiplexer_1_out, register_1_q, shift;

  buf or_1 (or_1_out, right);  // OR_Gate
  Register #(.width(5)) register_1 (.D(shift), .Q(register_1_q), .clk(or_1_out));  // open: en, clr
  Shifter #(.width(5), .shift("lr")) shifter_1 (.in(multiplexer_1_out), .\dist (3'b001), .out(shift));
  Comparator #(.width(5)) comparator_1 (.a({5{1'b0}}), .b(register_1_q), .eq(comparator_1_eq));  // open: gt, lt
  Multiplexer #(.width(5), .enable("false")) multiplexer_1 (
    .in0(register_1_q), .in1(5'b00100), .out(multiplexer_1_out), .sel(comparator_1_eq));
  Multiplexer #(.width(5), .enable("false")) multiplexer_2 (
    .in0(register_1_q), .in1(5'b00100), .out(out_2), .sel(comparator_1_eq));
  Comparator #(.width(5), .mode("unsigned")) comparator_2 (.a(5'b10000), .b(out_2), .eq(left_comp));  // open: gt, lt
endmodule
